// Logisim project alu.circ as structural Verilog: 12 circuits, main circuit main
module main (
  input  [3:0] in_1,
  input  [3:0] in_2
);

  _4_bit_full_adder u_4_bit_full_adder_1 ();  // open: A3, B3, A2, B2, A1, B1, A0, B0, Carry_In, Carry_Out, S3, S2, S1, S0
  _4_bit_substractor u_4_bit_substractor_1 ();  // open: Invert, A3, B3, A2, B2, A1, B1, A0, B0, Overflow___Underflow, S3, S2, S1, S0
  _4_bit_increment u_4_bit_increment_1 ();  // open: out_5, in_1, in_2, in_3, in_4, out_6, out_7, out_8, out_9
  _4_bit_decrementer u_4_bit_decrementer_1 ();  // open: A3, B3, A2, B2, A1, B1, A0, B0, Carry_Out, S3, S2, S1, S0
  _4_bit_right_left_shift u_4_bit_right_left_shift_1 ();  // open: Shift_Rigth, I3, I2, I1, I0, O3, O2, O1, O0, Shift_Left
  _4_bit_and u_4_bit_and_1 ();  // open: A3, B3, A2, B2, A1, B1, A0, B0, out_9, out_10, out_11, out_12
  _4_bit_or u_4_bit_or_1 ();  // open: A3, B3, A2, B2, A1, B1, A0, B0, out_9, out_10, out_11, out_12
  _4_bit_xor u_4_bit_xor_1 ();  // open: A3, B3, A2, B2, A1, B1, A0, B0, out_9, out_10, out_11, out_12
endmodule

// 1-bit Half\nAdder
module _1_bit_half_adder (
  input  A_In,
  input  B_In,
  output Sum_Out,
  output Carry_Out
);

  xor xor_1 (Sum_Out, A_In, B_In);
  and and_1 (Carry_Out, A_In, B_In);
endmodule

// 4 Bit Full Adder
module _4_bit_full_adder (
  input  A3,
  input  A2,
  input  A1,
  input  A0,
  input  B3,
  input  B2,
  input  B1,
  input  B0,
  input  Carry_In,
  output Carry_Out,
  output S3,
  output S2,
  output S1,
  output S0
);

  wire n1_bit_full_adder_2_carry_out, n1_bit_full_adder_3_carry_out, n1_bit_full_adder_4_carry_out;

  _1_bit_full_adder u_1_bit_full_adder_1 (
    .Carry_In(n1_bit_full_adder_2_carry_out), .A_In(A3), .B_In(B3), .Sum_Out(S3), .Carry_Out(Carry_Out));
  _1_bit_full_adder u_1_bit_full_adder_2 (
    .Carry_In(n1_bit_full_adder_3_carry_out), .A_In(A2), .B_In(B2), .Sum_Out(S2),
    .Carry_Out(n1_bit_full_adder_2_carry_out));
  _1_bit_full_adder u_1_bit_full_adder_3 (
    .Carry_In(n1_bit_full_adder_4_carry_out), .A_In(A1), .B_In(B1), .Sum_Out(S1),
    .Carry_Out(n1_bit_full_adder_3_carry_out));
  _1_bit_full_adder u_1_bit_full_adder_4 (
    .Carry_In(Carry_In), .A_In(A0), .B_In(B0), .Sum_Out(S0), .Carry_Out(n1_bit_full_adder_4_carry_out));
endmodule

// 1-Bit Full\nAdder
module _1_bit_full_adder (
  input  Carry_In,
  input  A_In,
  input  B_In,
  output Sum_Out,
  output Carry_Out
);

  wire n1_bit_half_adder_1_carry_out, n1_bit_half_adder_1_sum_out, n1_bit_half_adder_2_carry_out;

  _1_bit_half_adder u_1_bit_half_adder_1 (
    .A_In(A_In), .B_In(B_In), .Sum_Out(n1_bit_half_adder_1_sum_out), .Carry_Out(n1_bit_half_adder_1_carry_out));
  _1_bit_half_adder u_1_bit_half_adder_2 (
    .A_In(Carry_In), .B_In(n1_bit_half_adder_1_sum_out), .Sum_Out(Sum_Out),
    .Carry_Out(n1_bit_half_adder_2_carry_out));
  or or_1 (Carry_Out, n1_bit_half_adder_2_carry_out, n1_bit_half_adder_1_carry_out);
endmodule

// 4-Bit Subtractor
module _4_bit_substractor (
  input  B3,
  input  B2,
  input  B1,
  input  B0,
  input  Invert,
  input  A3,
  input  A2,
  input  A1,
  input  A0,
  output S3,
  output S2,
  output S1,
  output S0,
  output Overflow___Underflow
);

  wire n1_bit_full_adder_1_carry_out, n1_bit_full_adder_2_carry_out, n1_bit_full_adder_3_carry_out,
       n1_bit_full_adder_4_carry_out, ones_complement_1_o0, ones_complement_1_o1, ones_complement_1_o2,
       ones_complement_1_o3;

  xor xor_1 (Overflow___Underflow, Invert, n1_bit_full_adder_1_carry_out);
  _1_bit_full_adder u_1_bit_full_adder_1 (
    .Carry_In(n1_bit_full_adder_2_carry_out), .A_In(A3), .B_In(ones_complement_1_o3), .Sum_Out(S3),
    .Carry_Out(n1_bit_full_adder_1_carry_out));
  ones_complement ones_complement_1 (
    .I3(B3), .I2(B2), .I1(B1), .I0(B0), .O3(ones_complement_1_o3), .O2(ones_complement_1_o2),
    .O1(ones_complement_1_o1), .O0(ones_complement_1_o0), .Invert(Invert));
  _1_bit_full_adder u_1_bit_full_adder_2 (
    .Carry_In(n1_bit_full_adder_3_carry_out), .A_In(A2), .B_In(ones_complement_1_o2), .Sum_Out(S2),
    .Carry_Out(n1_bit_full_adder_2_carry_out));
  _1_bit_full_adder u_1_bit_full_adder_3 (
    .Carry_In(n1_bit_full_adder_4_carry_out), .A_In(A1), .B_In(ones_complement_1_o1), .Sum_Out(S1),
    .Carry_Out(n1_bit_full_adder_3_carry_out));
  _1_bit_full_adder u_1_bit_full_adder_4 (
    .Carry_In(Invert), .A_In(A0), .B_In(ones_complement_1_o0), .Sum_Out(S0),
    .Carry_Out(n1_bit_full_adder_4_carry_out));

  // Notes on the sheet:
  //   Carry In
endmodule

// 4- Bit One's Complement
module ones_complement (
  input  I3,
  input  I2,
  input  I1,
  input  I0,
  input  Invert,
  output O3,
  output O2,
  output O1,
  output O0
);

  xor xor_1 (O3, Invert, I3);
  xor xor_2 (O2, Invert, I2);
  xor xor_3 (O1, Invert, I1);
  xor xor_4 (O0, Invert, I0);
endmodule

// 4-Bit\nIncrementer
module _4_bit_increment (
  input  in_1,
  input  in_2,
  input  in_3,
  input  in_4,
  output out_5,
  output out_6,
  output out_7,
  output out_8,
  output out_9
);

  wire n1_bit_half_adder_2_carry_out, n1_bit_half_adder_3_carry_out, n1_bit_half_adder_4_carry_out;

  _1_bit_half_adder u_1_bit_half_adder_1 (
    .A_In(n1_bit_half_adder_2_carry_out), .B_In(in_1), .Sum_Out(out_6), .Carry_Out(out_5));
  _1_bit_half_adder u_1_bit_half_adder_2 (
    .A_In(n1_bit_half_adder_3_carry_out), .B_In(in_2), .Sum_Out(out_7),
    .Carry_Out(n1_bit_half_adder_2_carry_out));
  _1_bit_half_adder u_1_bit_half_adder_3 (
    .A_In(n1_bit_half_adder_4_carry_out), .B_In(in_3), .Sum_Out(out_8),
    .Carry_Out(n1_bit_half_adder_3_carry_out));
  _1_bit_half_adder u_1_bit_half_adder_4 (
    .A_In(1'b1), .B_In(in_4), .Sum_Out(out_9), .Carry_Out(n1_bit_half_adder_4_carry_out));
endmodule

// 4-Bit\nDecrementer
module _4_bit_decrementer (
  input  A3,
  input  A2,
  input  A1,
  input  A0,
  input  B3,
  input  B2,
  input  B1,
  input  B0,
  output Carry_Out,
  output S3,
  output S2,
  output S1,
  output S0
);

  wire n1_bit_full_adder_2_carry_out, n1_bit_full_adder_3_carry_out, n1_bit_full_adder_4_carry_out;

  _1_bit_full_adder u_1_bit_full_adder_1 (
    .Carry_In(n1_bit_full_adder_2_carry_out), .A_In(A3), .B_In(B3), .Sum_Out(S3), .Carry_Out(Carry_Out));
  _1_bit_full_adder u_1_bit_full_adder_2 (
    .Carry_In(n1_bit_full_adder_3_carry_out), .A_In(A2), .B_In(B2), .Sum_Out(S2),
    .Carry_Out(n1_bit_full_adder_2_carry_out));
  _1_bit_full_adder u_1_bit_full_adder_3 (
    .Carry_In(n1_bit_full_adder_4_carry_out), .A_In(A1), .B_In(B1), .Sum_Out(S1),
    .Carry_Out(n1_bit_full_adder_3_carry_out));
  _1_bit_full_adder u_1_bit_full_adder_4 (
    .Carry_In(1'b0), .A_In(A0), .B_In(B0), .Sum_Out(S0), .Carry_Out(n1_bit_full_adder_4_carry_out));
endmodule

// 4-Bit AND
module _4_bit_and (
  input  A3,
  input  A2,
  input  A1,
  input  A0,
  input  B3,
  input  B2,
  input  B1,
  input  B0,
  output out_9,
  output out_10,
  output out_11,
  output out_12
);

  and and_1 (out_9, A3, B3);
  and and_2 (out_10, A2, B2);
  and and_3 (out_11, A1, B1);
  and and_4 (out_12, A0, B0);
endmodule

// 4-Bit OR
module _4_bit_or (
  input  A3,
  input  A2,
  input  A1,
  input  A0,
  input  B3,
  input  B2,
  input  B1,
  input  B0,
  output out_9,
  output out_10,
  output out_11,
  output out_12
);

  or or_1 (out_9, A3, B3);
  or or_2 (out_10, A2, B2);
  or or_3 (out_11, A1, B1);
  or or_4 (out_12, A0, B0);
endmodule

// 4-Bit XOR
module _4_bit_xor (
  input  A3,
  input  A2,
  input  A1,
  input  A0,
  input  B3,
  input  B2,
  input  B1,
  input  B0,
  output out_9,
  output out_10,
  output out_11,
  output out_12
);

  xor xor_1 (out_9, A3, B3);
  xor xor_2 (out_10, A2, B2);
  xor xor_3 (out_11, A1, B1);
  xor xor_4 (out_12, A0, B0);
endmodule

// 4-Bit\nRight/Left Shift
module _4_bit_right_left_shift (
  input  I3,
  input  I2,
  input  I1,
  input  I0,
  input  Shift_Left,
  input  Shift_Rigth,
  output O3,
  output O2,
  output O1,
  output O0
);

  wire and_1_out, and_2_out, and_3_out, and_4_out, and_5_out, and_6_out, and_7_out, and_8_out, and_9_out,
       and_10_out, and_11_out, and_12_out, not_1_out, not_2_out, not_3_out, not_4_out, not_5_out, not_6_out,
       not_7_out, not_8_out;

  and and_1 (and_1_out, Shift_Rigth, 1'b0);
  not not_1 (not_1_out, Shift_Rigth);
  and and_2 (and_2_out, I3, not_1_out, not_2_out);
  or or_1 (O3, and_1_out, and_2_out, and_3_out);
  not not_2 (not_2_out, Shift_Left);
  and and_3 (and_3_out, Shift_Left, I2);
  and and_4 (and_4_out, Shift_Rigth, I3);
  not not_3 (not_3_out, Shift_Rigth);
  and and_5 (and_5_out, I2, not_3_out, not_4_out);
  or or_2 (O2, and_4_out, and_5_out, and_6_out);
  not not_4 (not_4_out, Shift_Left);
  and and_6 (and_6_out, Shift_Left, I1);
  and and_7 (and_7_out, Shift_Rigth, I2);
  not not_5 (not_5_out, Shift_Rigth);
  and and_8 (and_8_out, I1, not_5_out, not_6_out);
  or or_3 (O1, and_7_out, and_8_out, and_9_out);
  not not_6 (not_6_out, Shift_Left);
  and and_9 (and_9_out, Shift_Left, I0);
  and and_10 (and_10_out, Shift_Rigth, I1);
  not not_7 (not_7_out, Shift_Rigth);
  and and_11 (and_11_out, I0, not_7_out, not_8_out);
  or or_4 (O0, and_10_out, and_11_out, and_12_out);
  not not_8 (not_8_out, Shift_Left);
  and and_12 (and_12_out, Shift_Left, 1'b0);
endmodule
